# Fritzing sketch NasaProjeto (saved by Fritzing 0.9.3b)

parts:
  D_O_Circuit1 = D.O. Circuit
  Pre-Assembled_Female_BNC1 = Pre-Assembled Female BNC  # not connected
  Componente1 = Arduino Uno (Rev3)

nets:
  GND: D_O_Circuit1.GND, Componente1.GND
  N1: D_O_Circuit1.TX, Componente1.D2
  N2: D_O_Circuit1.RX, Componente1.D3_PWM
