# Fritzing sketch NasaProjeto1 (saved by Fritzing 0.9.3b)

parts:
  D_O_Circuit1 = D.O. Circuit
  Pre-Assembled_Female_BNC1 = Pre-Assembled Female BNC
  Componente1 = Arduino Uno (Rev3)

nets:
  N1: D_O_Circuit1.GND#0, Componente1.GND
  N2: D_O_Circuit1.TX, Componente1.D2
  N3: D_O_Circuit1.RX, Componente1.D3_PWM
  VCC: D_O_Circuit1.Vcc, Componente1.5V
  N4: D_O_Circuit1.PRB, Pre-Assembled_Female_BNC1.PRB
  N5: D_O_Circuit1.GND#5, Pre-Assembled_Female_BNC1.GND
